# Fritzing sketch led (saved by Fritzing 1.0.0rc)
breadboards: 1

parts:
  Εξάρτημα1 = Arduino Uno (Rev3)
  LED1 = smd LED [color="Red (633nm)" package="0603 [SMD]"]
  R1 = Resistor [tolerance=±5% power=0.25 resistance=220 package=THT]

nets:
  N1: Εξάρτημα1.D7, R1.Pin_1
  N2: Εξάρτημα1.GND, LED1.cathode
  N3: LED1.anode, R1.Pin_0
